// Logisim project hw3.circ as structural Verilog: 6 circuits, main circuit SR_Latch
module SR_Latch (
  input  in_1,
  input  in_2,
  output out_3,
  output out_4
);

  wire or_1_out, or_2_out;

  or or_1 (or_1_out, in_1, out_4);
  or or_2 (or_2_out, out_3, in_2);
  not not_1 (out_3, or_1_out);
  not not_2 (out_4, or_2_out);

  // Notes on the sheet:
  //   Provided for you
endmodule

module D_Latch (
  input  in_1,
  input  in_2,
  output out_3
);

  wire and_1_out, and_2_out, not_1_out;

  not not_1 (not_1_out, in_1);
  and and_1 (and_1_out, in_1, in_2);
  and and_2 (and_2_out, not_1_out, in_2);
  SR_Latch SR (.in_1(and_1_out), .in_2(and_2_out), .out_4(out_3));  // open: out_3

  // Notes on the sheet:
  //   Strobe
  //   Provided for you
  //   We ignore the NOT Q output
endmodule

module Decoder (
  input  in_1,
  input  in_2,
  output out_3,
  output out_4,
  output out_5,
  output out_6
);

  wire not_1_out, not_2_out, not_3_out, not_4_out;

  not not_1 (not_1_out, in_1);
  not not_2 (not_2_out, in_2);
  not not_3 (not_3_out, in_1);
  not not_4 (not_4_out, in_2);
  and and_1 (out_3, not_1_out, not_2_out);
  and and_2 (out_4, not_3_out, in_2);
  and and_3 (out_5, in_1, not_4_out);
  and and_4 (out_6, in_1, in_2);

  // Notes on the sheet:
  //   Provided for you
endmodule

module RAM (
  input  in_1,
  input  _2Bit_Addr,
  input  in_3,
  input  _3Bit_Data,
  input  in_5,
  input  Write,
  output out_7,
  output out_8,
  output out_9
);

  wire A00_out_5, A00_out_6, A00_out_7, A01_out_5, A01_out_6, A01_out_7, A10_out_5, A10_out_6, A10_out_7,
       A11_out_5, A11_out_6, A11_out_7, and_1_out, and_2_out, and_3_out, and_4_out, d_latch_1_out_3,
       d_latch_2_out_3, d_latch_3_out_3, d_latch_4_out_3, d_latch_5_out_3, d_latch_6_out_3, d_latch_7_out_3,
       d_latch_8_out_3, d_latch_9_out_3, d_latch_10_out_3, d_latch_11_out_3, d_latch_12_out_3,
       decoder_1_out_3, decoder_1_out_4, decoder_1_out_5, decoder_1_out_6;

  Decoder decoder_1 (
    .out_3(decoder_1_out_3), .out_4(decoder_1_out_4), .out_5(decoder_1_out_5), .out_6(decoder_1_out_6),
    .in_2(_2Bit_Addr), .in_1(in_1));
  and and_1 (and_1_out, decoder_1_out_3, Write);
  and and_2 (and_2_out, decoder_1_out_4, Write);
  and and_3 (and_3_out, decoder_1_out_5, Write);
  and and_4 (and_4_out, decoder_1_out_6, Write);
  D_Latch d_latch_1 (.out_3(d_latch_1_out_3), .in_1(in_3), .in_2(and_1_out));
  D_Latch d_latch_2 (.out_3(d_latch_2_out_3), .in_1(in_3), .in_2(and_2_out));
  D_Latch d_latch_3 (.out_3(d_latch_3_out_3), .in_1(in_3), .in_2(and_3_out));
  D_Latch d_latch_4 (.out_3(d_latch_4_out_3), .in_1(in_3), .in_2(and_4_out));
  D_Latch d_latch_5 (.out_3(d_latch_5_out_3), .in_1(_3Bit_Data), .in_2(and_1_out));
  D_Latch d_latch_6 (.out_3(d_latch_6_out_3), .in_1(_3Bit_Data), .in_2(and_2_out));
  D_Latch d_latch_7 (.out_3(d_latch_7_out_3), .in_1(_3Bit_Data), .in_2(and_3_out));
  D_Latch d_latch_8 (.out_3(d_latch_8_out_3), .in_1(_3Bit_Data), .in_2(and_4_out));
  D_Latch d_latch_9 (.out_3(d_latch_9_out_3), .in_1(in_5), .in_2(and_1_out));
  D_Latch d_latch_10 (.out_3(d_latch_10_out_3), .in_1(in_5), .in_2(and_2_out));
  D_Latch d_latch_11 (.out_3(d_latch_11_out_3), .in_1(in_5), .in_2(and_3_out));
  D_Latch d_latch_12 (.out_3(d_latch_12_out_3), .in_1(in_5), .in_2(and_4_out));
  Address A00 (
    .A(decoder_1_out_3), .B1(d_latch_1_out_3), .B2(d_latch_5_out_3), .B3(d_latch_9_out_3), .out_5(A00_out_5),
    .out_6(A00_out_6), .out_7(A00_out_7));
  Address A01 (
    .A(decoder_1_out_4), .B1(d_latch_2_out_3), .B2(d_latch_6_out_3), .B3(d_latch_10_out_3),
    .out_5(A01_out_5), .out_6(A01_out_6), .out_7(A01_out_7));
  Address A10 (
    .A(decoder_1_out_5), .B1(d_latch_11_out_3), .B2(d_latch_7_out_3), .B3(d_latch_3_out_3),
    .out_5(A10_out_5), .out_6(A10_out_6), .out_7(A10_out_7));
  Address A11 (
    .A(decoder_1_out_6), .B1(d_latch_12_out_3), .B2(d_latch_8_out_3), .B3(d_latch_4_out_3),
    .out_5(A11_out_5), .out_6(A11_out_6), .out_7(A11_out_7));
  or or_1 (out_7, A10_out_5, A01_out_5, A00_out_5, A11_out_5);
  or or_2 (out_8, A00_out_6, A01_out_6, A10_out_6, A11_out_6);
  or or_3 (out_9, A00_out_7, A01_out_7, A10_out_7, A11_out_7);

  // Notes on the sheet:
  //   Name:
  //   Pledge:
  //   Implement  3 Bit, 4 Word RAM
  //   Issac Zheng
  //   Implement the WRITE operation
  //   If you need help, look at slides 9-16 in week9.pdf
  //   The 3 Bit Output should reflect the values stored in the word selected by the 2Bit Addr
  //   I pledge my honor that I have abided by the Stevens Honor System.
endmodule

module Remainder (
  input  a,
  input  b,
  input  c,
  input  x,
  input  y,
  output n,
  output m,
  output out_8
);

  wire a_prime_b_prime_c_out, a_prime_bc_prime_out, ab_prime_c_out, ab_prime_c_prime_out, abc_out, c_out,
       decoder_1_out_5, decoder_1_out_6, not_1_out, not_2_out, not_3_out, or_2_out;

  not not_1 (not_1_out, a);
  not not_2 (not_2_out, b);
  not not_3 (not_3_out, c);
  Decoder decoder_1 (
    .out_3(out_8), .out_5(decoder_1_out_5), .out_6(decoder_1_out_6), .in_2(y), .in_1(x));  // open: out_4
  and a_prime_bc_prime (a_prime_bc_prime_out, decoder_1_out_6, not_3_out, b, not_1_out);
  and ab_prime_c (ab_prime_c_out, a, not_2_out, c, decoder_1_out_6);
  and u_c (c_out, c, decoder_1_out_5);
  or or_1 (n, a_prime_bc_prime_out, ab_prime_c_out);
  and abc (abc_out, a, b, c, decoder_1_out_6);
  and a_prime_b_prime_c (a_prime_b_prime_c_out, not_1_out, c, not_2_out, decoder_1_out_6);
  and ab_prime_c_prime (ab_prime_c_prime_out, a, not_3_out, not_2_out, decoder_1_out_6);
  or or_2 (or_2_out, abc_out, a_prime_b_prime_c_out, ab_prime_c_prime_out);
  or or_3 (m, or_2_out, c_out);

  // Notes on the sheet:
  //   Numerator
  //   Divisor
  //   xy
  //   xy'
  //   Part 2: Create a circuit to calculate remainders, given a 3-bit numerator and 2-bit divisor.
  //   (Hint: You may want to write a truth table first)
  //   xy
  //   Remainder
  //   Error bit (Set when division isn't possible)
endmodule

module Address (
  input  A,
  input  B1,
  input  B2,
  input  B3,
  output out_5,
  output out_6,
  output out_7
);

  and and_1 (out_5, A, B1);
  and and_2 (out_6, A, B2);
  and and_3 (out_7, A, B3);
endmodule
