// Logisim project lab8.circ as structural Verilog: 2 circuits, main circuit ParityGenerator
module XOR (
  input  X,
  input  Y,
  output out_3
);


  // Notes on the sheet:
  //   Use minterm expansion to create an XOR gate using AND + OR gates
endmodule

module ParityGenerator (
  input  X,
  input  Y,
  input  Z,
  output Parity
);

  wire and_1_out, and_2_out, and_3_out, and_5_out, and_6_out, not_1_out, not_2_out, not_3_out, or_1_out,
       or_2_out, or_3_out;

  not not_1 (not_1_out, and_1_out);
  and and_1 (and_1_out, Z, Y);
  or or_1 (or_1_out, Z, Y);
  and and_2 (and_2_out, not_1_out, or_1_out);
  and and_3 (and_3_out, and_2_out, X);
  or or_2 (or_2_out, and_2_out, X);
  not not_2 (not_2_out, and_3_out);
  // Probe on Parity
  and and_4 (Parity, not_2_out, or_2_out);
  // AND_Gate and_5 has open pins: out=and_5_out
  // OR_Gate or_3 has open pins: out=or_3_out
  not not_3 (not_3_out, and_5_out);
  and and_6 (and_6_out, not_3_out, or_3_out);

  // Notes on the sheet:
  //   Input Bits
  //   Output Bit
  //   Write your parity circuit here
  //   the output = 1 if an odd number of inputs (1 or 3) are 1, otherwise 0
  //   ONLY use: NOT, AND, OR, and any custom functions you write (included in the .circ submission)
  //   WRITE YOUR NAME AND PLEDGE SOMEWHERE IN THIS CIRCUIT
  //   Issac Zheng
  //   I pledge my honor that I have abided by the Stevens Honor System.
  //   XOR Circuit
endmodule
