// Logisim project lab9.circ as structural Verilog: 4 circuits, main circuit D_Latch
module NOR (
  input  X,
  input  Y,
  output Out
);

  wire or_1_out;

  or or_1 (or_1_out, X, Y);
  not not_1 (Out, or_1_out);

  // Notes on the sheet:
  //   NOR
  //   Using only OR and NOT gates, please create the NOR gate
  //   This gate returns 1 if both bits are 0, and 0 otherwise
endmodule

module TwoBit_Decoder (
  input  Input0,
  input  Input1,
  output Output0,
  output Output1,
  output Ouput2,
  output Ouput3
);

  wire not_1_out, not_2_out, not_3_out, not_4_out;

  not not_1 (not_1_out, Input1);
  not not_2 (not_2_out, Input0);
  not not_3 (not_3_out, Input0);
  not not_4 (not_4_out, Input1);
  and and_1 (Output0, not_1_out, not_2_out);
  and and_2 (Output1, Input1, not_3_out);
  and and_3 (Ouput2, not_4_out, Input0);
  and and_4 (Ouput3, Input1, Input0);

  // Notes on the sheet:
  //   2 Bit Decoder
  //   00 should turn on Output0 and nothing else
  //   01 should turn on Output1 and nothing else
  //   10 should turn on Output2 and nothing else
  //   11 should turn on Output3 and nothing else
  //   Using only AND and NOT gates, please write this decoder circuit
  //   Consider the input 01 to mean Input0 is 0, Input1 is 1.
endmodule

module SR_Latch (
  input  S,
  input  R,
  output Q
);

  wire nor_1_out;

  NOR nor_1 (.Out(nor_1_out), .Y(S), .X(Q));
  NOR nor_2 (.Out(Q), .Y(nor_1_out), .X(R));

  // Notes on the sheet:
  //   Q: pull=up
  //   R: pull=down
  //   S: pull=down
  //   S-R Latch
  //   Using two of the NOR gate you just wrote, create an S-R latch
  //   The behavior of this circuit is not defined if both S and R are on
  //   Notice that in the SR=00 state, the output Q could be either 0 or 1 !  
  //   Logism will also throw this error every time you open a successfully built latch's .circ file
  //   In this circuit, each input feeds one NOR gate, and the output of each NOR gate loops intp the other input's gate
  //   This makes the latch different from any circuit you've worked with before, and the basis for computer memory.
  //   If your wires turn red and Logism yells at you for apparent oscillation, you've messed something up.
  //   Then, draw your loop back in and it should function properly. If not, go to someone's office hours.
  //   The output should become 1 when S is turned on, 0 when R is turned on, and remain whatever it is if both are turned off
  //   To fix this, break any loop in your circuit, then in the Simulate menu up top turn "Simulation Enabled" on and off again
endmodule

module D_Latch (
  input  D,
  input  Strobe,
  input  D_2,
  input  Strobe_2,
  output Output,
  output Output_2
);

  wire and_1_out, and_2_out, and_3_out, and_4_out, nor_1_out, nor_2_out, not_1_out, not_2_out;

  not not_1 (not_1_out, D);
  NOR nor_1 (.Out(nor_1_out), .Y(and_3_out), .X(Output_2));
  not not_2 (not_2_out, D_2);
  NOR nor_2 (.Out(nor_2_out), .Y(and_1_out), .X(Output));
  and and_1 (and_1_out, D, Strobe);
  and and_2 (and_2_out, not_1_out, Strobe);
  NOR nor_3 (.Out(Output), .Y(nor_2_out), .X(and_2_out));
  and and_3 (and_3_out, D_2, Strobe_2);
  and and_4 (and_4_out, not_2_out, Strobe_2);
  NOR nor_4 (.Out(Output_2), .Y(and_4_out), .X(nor_1_out));

  // Notes on the sheet:
  //   Prototype
  //   D Latch
  //   Issac Zheng
  //   Write your name and pledge here
  //   Your circuit should use 2 NOR gates, 2 AND gates, and 1 NOT. 
  //   If Strobe is 1, then the value of output should become the value of D
  //   This avoids the situation where both S and R are on
  //   The whole oscillation deal also applies here - be ready to fight Logism
  //   I pledge my honor that I have abided by the Stevens Honor System.
  //   The D latch improves on the S-R by having one input, D, and a Strobe.
  //   If Strobe is 0, then the value of D should have no impact at all on the output bit
  //   If Strobe is 0, you need to stop any inputs to your S-R latch, consider how to do that
  //   D will feed eventually into both S and R inputs to the S-R latch, just invert one of them
  //   The S-R latch we just designed has several flaws, such as both S and R being 1 not having defined output
  //   This is accomplished with an S-R latch as part of the D latch - do not drag in your pre-built SR latch, create it anew!
  //   Hint: Check out week9.pdf
endmodule
